# Fritzing sketch board_layout (saved by Fritzing 0.9.8b)
perfboards: 1

parts:
  J6 = male pin header, 3 pins [form="♂ (male)"]  # not connected
  J7 = female pin header, 10 pins [form="♀ (female)"]
  J8 = female pin header, 15 pins [form="♀ (female)"]  # not connected
  J9 = female pin header, 15 pins [form="♀ (female)"]

nets:
  N1: J7.pin6, J7.pin9, J9.pin2
  N2: J7.pin7, J9.pin12
  N3: J7.pin8, J9.pin14

notes:
  ADS115
  PH Meter
  DC Power
  ESP 32
